# Fritzing sketch LED_Dimmer_Fritzing (saved by Fritzing 0.9.5d)

parts:
  J1 = STM32 Nucleo boards
  LED_Dimmer = LED - 5mm [color="Green (555nm)" package="5 mm [THT]"]  # not connected
  Rotary_Sensor = Rotary Potentiometer (Small) [maximum_resistance=100kΩ package=THT]

nets:
  N1: J1.A1, Rotary_Sensor.wiper
  N2: J1.5V, Rotary_Sensor.leg2
  N3: J1.GND, Rotary_Sensor.leg1
